// Logisim project avaliador_condicao.circ as structural Verilog: 1 circuit, main circuit AvaliadorCondicao
module AvaliadorCondicao (
  input  [3:0] NZCV,
  input  [3:0] cond,
  output cond_pass
);

  PLA #(.in_width(8), .out_width(1), .\table ("0000x1xx 1 # EQ\n0001x0xx 1 # NE\n0010xx1x 1 # CS_HS\n0011xx0x 1 # CC_LO\n01001xxx 1 # MI\n01010xxx 1 # PL\n0110xxx1 1 # VS\n0111xxx0 1 # VC\n1000x01x 1 # HI\n1001xx0x 1 # LS_a\n1001x1xx 1 # LS_b\n10101xx1 1 # GE_a\n10100xx0 1 # GE_b\n10111xx0 1 # LT_a\n10110xx1 1 # LT_b\n110010x1 1 # GT_a\n110000x0 1 # GT_b\n1101x1xx 1 # LE_a\n11011xx0 1 # LE_b\n11010xx1 1 # LE_c\n1110xxxx 1 # AL\n1111xxxx 1 # cond11110110---1")) pla_1 (
    .in({cond, NZCV}), .out(cond_pass));
endmodule
