// Logisim project cpu_microprogramada.circ as structural Verilog: 10 circuits, main circuit ALU
module main (
);

  wire CLK, controlunit_1_alusrc, controlunit_1_memtoreg, controlunit_1_memwrite, controlunit_1_pcsrc,
       controlunit_1_r2orimmtoreg, controlunit_1_regwrite, RESET;
  wire [0:0] controlunit_1_regsrc;
  wire [1:0] controlunit_1_immsrc, controlunit_1_regsrc_2;
  wire [2:0] controlunit_1_alucontrol;
  wire [3:0] aluw_flags_7d6c4d71_1_aluflags, multiplexer_2_out, multiplexer_3_out;
  wire [23:0] adder_1_out, adder_2_out, multiplexer_4_out, nextpc_1_nexpc, PC_q;
  wire [31:0] aluw_flags_7d6c4d71_1_result, bit_extender_1_out, extender_1_out, ir_1_q, multiplexer_5_out,
       multiplexer_6_out, ram_1_dout, REG_rd1, REG_rd2, rom_1_data, shifter_1_out;
  wire [31:24] multiplexer_4_out_2;

  Clock clock_1 (.out(CLK));
  Button button_1 (.out(RESET));
  Multiplexer #(.width(24)) multiplexer_1 (
    .in0(multiplexer_4_out), .in1(adder_1_out), .sel(controlunit_1_pcsrc));  // open: out
  Register #(.width(24)) PC (.D(nextpc_1_nexpc), .clk(CLK), .Q(PC_q), .clr(RESET));  // open: en
  ROM #(.addrWidth(24), .dataWidth(32)) rom_1 (.addr(PC_q), .data(rom_1_data));
  Adder #(.width(24)) adder_1 (.a(PC_q), .b(24'h1), .out(adder_1_out));  // open: cin, cout
  Adder #(.width(24)) adder_2 (.a(adder_1_out), .b(24'h2), .out(adder_2_out));  // open: cin, cout
  assign bit_extender_1_out = {{8{adder_2_out[23]}}, adder_2_out};  // Bit_Extender bit_extender_1
  ControlUnit controlunit_1 (
    .Funct(ir_1_q[25:20]), .Shift(ir_1_q[6:4]), .CLK(CLK), .Cond(ir_1_q[31:28]), .Rd(ir_1_q[15:12]),
    .Opt(ir_1_q[27:26]), .Flags(aluw_flags_7d6c4d71_1_aluflags), .R2orImmtoReg(controlunit_1_r2orimmtoreg),
    .ALUSrc(controlunit_1_alusrc), .MemtoReg(controlunit_1_memtoreg),
    .RegSrc({controlunit_1_regsrc_2, controlunit_1_regsrc[0]}), .MemWrite(controlunit_1_memwrite),
    .RegWrite(controlunit_1_regwrite), .PCSrc(controlunit_1_pcsrc), .ImmSrc(controlunit_1_immsrc),
    .ALUControl(controlunit_1_alucontrol));  // open: cond_pass_dbg
  Multiplexer #(.select(2), .width(4)) multiplexer_2 (
    .in0(ir_1_q[19:16]), .in1(4'b1111), .in2(ir_1_q[3:0]), .out(multiplexer_2_out),
    .sel(controlunit_1_regsrc_2));  // open: in3
  Multiplexer #(.width(4)) multiplexer_3 (
    .in0(ir_1_q[3:0]), .in1(ir_1_q[15:12]), .out(multiplexer_3_out), .sel(controlunit_1_regsrc[0]));
  IR ir_1 (.CLK(CLK), .D(rom_1_data), .IRWrite(1'b1), .Q(ir_1_q));
  RegisterField REG (
    .WE3(controlunit_1_regwrite), .A3(ir_1_q[15:12]), .R15(bit_extender_1_out),
    .WD3({multiplexer_4_out_2, multiplexer_4_out}), .Reset(RESET), .A1(multiplexer_2_out),
    .A2(multiplexer_3_out), .CLK(CLK), .RD1(REG_rd1), .RD2(REG_rd2));  // open: PINR1, PINR7, PINR2, PINR8, PINR3, PINR9, PINR13, PINR4, PINR10, PINR14, PINR11, PINR5, PINR15, PINR6, PINR12
  Extender extender_1 (.In(ir_1_q[23:0]), .ImmSrc(controlunit_1_immsrc), .Out(extender_1_out));
  Shifter shifter_1 (.A(REG_rd2), .Width(ir_1_q[11:7]), .ShiftCtrl(ir_1_q[6:5]), .Out(shifter_1_out));
  Multiplexer #(.width(32)) multiplexer_4 (
    .in0(multiplexer_6_out), .in1(multiplexer_5_out), .out({multiplexer_4_out_2, multiplexer_4_out}),
    .sel(controlunit_1_r2orimmtoreg));
  Multiplexer #(.width(32)) multiplexer_5 (
    .in0(shifter_1_out), .in1(extender_1_out), .out(multiplexer_5_out), .sel(controlunit_1_alusrc));
  ALUw_Flags_7d6c4d71 aluw_flags_7d6c4d71_1 (
    .B(multiplexer_5_out), .A(REG_rd1), .ALUControl(controlunit_1_alucontrol),
    .ALUFlags(aluw_flags_7d6c4d71_1_aluflags), .Result(aluw_flags_7d6c4d71_1_result));
  NextPC nextpc_1 (
    .PC(PC_q), .PCPlus1(adder_1_out), .BranchTarget(aluw_flags_7d6c4d71_1_result[23:0]), .Extra({24{1'b0}}),
    .NexPC(nextpc_1_nexpc));  // open: Sel0, Sel1
  Multiplexer #(.width(32)) multiplexer_6 (
    .in0(aluw_flags_7d6c4d71_1_result), .in1(ram_1_dout), .out(multiplexer_6_out),
    .sel(controlunit_1_memtoreg));
  RAM #(.addrWidth(24), .dataWidth(32)) ram_1 (
    .addr(aluw_flags_7d6c4d71_1_result[23:0]), .we(controlunit_1_memwrite), .clk(CLK), .din(REG_rd2),
    .dout(ram_1_dout));  // open: oe

  // Notes on the sheet:
  //   PCPlus1
  //   contents of rom_1 (hex, n*v repeats v):
  //   e3a01006 e3a02005 e3a04001 e0813002 e1a03083 e0533004 e2855001 1afffffc eafffffe
  //   PCPlus2
endmodule

module ALU (
  input  [1:0] ALUControl,
  input  [31:0] B,
  input  [31:0] A,
  output [31:0] Result
);

  wire [31:0] adder_1_out, and_1_out, multiplexer_1_out, not_1_out, or_1_out;

  Multiplexer #(.width(32)) multiplexer_1 (.in0(B), .in1(not_1_out), .out(multiplexer_1_out), .sel(ALUControl[0]));
  assign not_1_out = ~B;  // NOT_Gate not_1, 32 bits wide
  Adder #(.width(32)) adder_1 (.a(multiplexer_1_out), .b(A), .out(adder_1_out), .cin(ALUControl[0]));  // open: cout
  assign and_1_out = B & A;  // AND_Gate and_1, 32 bits wide
  assign or_1_out = B | A;  // OR_Gate or_1, 32 bits wide
  Multiplexer #(.select(2), .width(32)) multiplexer_2 (
    .in0(adder_1_out), .in1(adder_1_out), .in2(and_1_out), .in3(or_1_out), .out(Result), .sel(ALUControl));
endmodule

module RegisterField (
  input  CLK,
  input  Reset,
  input  [3:0] A1,
  input  [3:0] A2,
  input  [3:0] A3,
  input  WE3,
  input  [31:0] WD3,
  input  [31:0] R15,
  output [31:0] PINR1,
  output [31:0] PINR2,
  output [31:0] PINR3,
  output [31:0] PINR4,
  output [31:0] PINR5,
  output [31:0] PINR6,
  output [31:0] PINR7,
  output [31:0] PINR8,
  output [31:0] PINR9,
  output [31:0] PINR10,
  output [31:0] PINR11,
  output [31:0] PINR12,
  output [31:0] RD1,
  output [31:0] PINR13,
  output [31:0] PINR14,
  output [31:0] PINR15,
  output [31:0] RD2
);

  wire demultiplexer_1_out4, demultiplexer_1_out5, demultiplexer_1_out6, demultiplexer_1_out7,
       demultiplexer_1_out8, demultiplexer_1_out9, demultiplexer_1_out10, demultiplexer_1_out11,
       demultiplexer_1_out12, demultiplexer_1_out13, demultiplexer_1_out14;

  Demultiplexer #(.select(4)) demultiplexer_1 (
    .out0(CLK), .out1(CLK), .out2(CLK), .out3(CLK), .out4(demultiplexer_1_out4), .out5(demultiplexer_1_out5),
    .out6(demultiplexer_1_out6), .out7(demultiplexer_1_out7), .out8(demultiplexer_1_out8),
    .out9(demultiplexer_1_out9), .out10(demultiplexer_1_out10), .out11(demultiplexer_1_out11),
    .out12(demultiplexer_1_out12), .out13(demultiplexer_1_out13), .out14(demultiplexer_1_out14), .in(WE3),
    .sel(A3));  // open: out15
  Register #(.width(32)) r0 (.D(WD3), .en(CLK), .clk(CLK), .Q(PINR1), .clr(Reset));
  Register #(.width(32)) r4 (.D(WD3), .en(demultiplexer_1_out4), .clk(CLK), .Q(PINR5), .clr(Reset));
  Register #(.width(32)) r8 (.D(WD3), .en(demultiplexer_1_out8), .clk(CLK), .Q(PINR9), .clr(Reset));
  Register #(.width(32)) r12 (.D(WD3), .en(demultiplexer_1_out12), .clk(CLK), .Q(PINR13), .clr(Reset));
  Register #(.width(32)) r1 (.D(WD3), .en(CLK), .clk(CLK), .Q(PINR2), .clr(Reset));
  Register #(.width(32)) r5 (.D(WD3), .en(demultiplexer_1_out5), .clk(CLK), .Q(PINR6), .clr(Reset));
  Register #(.width(32)) r9 (.D(WD3), .en(demultiplexer_1_out9), .clk(CLK), .Q(PINR10), .clr(Reset));
  Register #(.width(32)) r13 (.D(WD3), .en(demultiplexer_1_out13), .clk(CLK), .Q(PINR14), .clr(Reset));
  Register #(.width(32)) r2 (.D(WD3), .en(CLK), .clk(CLK), .Q(PINR3), .clr(Reset));
  Register #(.width(32)) r6 (.D(WD3), .en(demultiplexer_1_out6), .clk(CLK), .Q(PINR7), .clr(Reset));
  Register #(.width(32)) r10 (.D(WD3), .en(demultiplexer_1_out10), .clk(CLK), .Q(PINR11), .clr(Reset));
  Register #(.width(32)) r7 (.D(WD3), .en(demultiplexer_1_out7), .clk(CLK), .Q(PINR8), .clr(Reset));
  Register #(.width(32)) r11 (.D(WD3), .en(demultiplexer_1_out11), .clk(CLK), .Q(PINR12), .clr(Reset));
  Register #(.width(32)) r14 (.D(WD3), .en(demultiplexer_1_out14), .clk(CLK), .Q(PINR15), .clr(Reset));
  Register #(.width(32)) r3 (.D(WD3), .en(CLK), .clk(CLK), .Q(PINR4), .clr(Reset));
  Multiplexer #(.select(4), .width(32)) multiplexer_1 (
    .in0(PINR1), .in1(PINR2), .in2(PINR3), .in3(PINR4), .in4(PINR5), .in5(PINR6), .in6(PINR7), .in7(PINR8),
    .in8(PINR9), .in9(PINR10), .in10(PINR11), .in11(PINR12), .in12(PINR13), .in13(PINR14), .in14(PINR15),
    .in15(R15), .out(RD1), .sel(A1));
  Multiplexer #(.select(4), .width(32)) multiplexer_2 (
    .in0(PINR1), .in1(PINR2), .in2(PINR3), .in3(PINR4), .in4(PINR5), .in5(PINR6), .in6(PINR7), .in7(PINR8),
    .in8(PINR9), .in9(PINR10), .in10(PINR11), .in11(PINR12), .in12(PINR13), .in13(PINR14), .in14(PINR15),
    .in15(R15), .out(RD2), .sel(A2));
endmodule

module ControlUnit (
  input  CLK,
  input  [1:0] Opt,
  input  [3:0] Cond,
  input  [2:0] Shift,
  input  [3:0] Rd,
  input  [3:0] Flags,
  input  [5:0] Funct,
  output MemtoReg,
  output PCSrc,
  output [2:0] RegSrc,
  output [2:0] ALUControl,
  output cond_pass_dbg,
  output R2orImmtoReg,
  output ALUSrc,
  output [1:0] ImmSrc,
  output MemWrite,
  output RegWrite
);

  wire BR, BRANY, EN_CV, EN_NZ, MW, ORB0, ORB1, RD15, RW, SFI, WPC15;
  wire [1:0] CVQ, FLAGW;
  wire [2:0] ALUC_ROM;
  wire [3:2] NZCV;
  wire [5:0] UADDR;
  wire [29:17] UWORD;

  PLA #(.in_width(8), .out_width(6), .\table ("00001000 000001 # ADD reg\n00001001 000010 # ADDS reg\n00101000 000011 # ADD imm\n00101001 000100 # ADDS imm\n00000100 000101 # SUB reg\n00000101 000110 # SUBS reg\n00100100 000111 # SUB imm\n00100101 001000 # SUBS imm\n00000000 001001 # AND reg\n00000001 001010 # ANDS reg\n00100000 001011 # AND imm\n00100001 001100 # ANDS imm\n00011000 001101 # ORR reg\n00011001 001110 # ORRS reg\n00111000 001111 # ORR imm\n00111001 010000 # ORRS imm\n00111010 010001 # MOV imm\n00111011 010010 # MOVS imm\n00011010 010011 # MOV reg\n00011011 010100 # MOVS reg\n00010101 010101 # CMP reg\n00110101 010110 # CMP imm\n01xx1xx1 010111 # LDR U=1 (soma offset)\n01xx0xx1 011010 # LDR U=0 (subtrai offset)\n01xx1xx0 011000 # STR U=1 (soma offset)\n01xx0xx0 011011 # STR U=0 (subtrai offset)\n101xxxxx 011001 # B/Bcc")) Dispatch (
    .in({Opt, Funct}), .out(UADDR));
  PLA #(.in_width(8), .out_width(1), .\table ("0000x1xx 1 # EQ\n0001x0xx 1 # NE\n0010xx1x 1 # CS_HS\n0011xx0x 1 # CC_LO\n01001xxx 1 # MI\n01010xxx 1 # PL\n0110xxx1 1 # VS\n0111xxx0 1 # VC\n1000x01x 1 # HI\n1001xx0x 1 # LS_a\n1001x1xx 1 # LS_b\n10101xx1 1 # GE_a\n10100xx0 1 # GE_b\n10111xx0 1 # LT_a\n10110xx1 1 # LT_b\n110010x1 1 # GT_a\n110000x0 1 # GT_b\n1101x1xx 1 # LE_a\n11011xx0 1 # LE_b\n11010xx1 1 # LE_c\n1110xxxx 1 # AL\n1111xxxx 1 # cond1111")) CondPLA (
    .in({Cond, NZCV, CVQ}), .out(cond_pass_dbg));
  and and_1 (RD15, Rd[0], Rd[1], Rd[2], Rd[3]);
  and and_2 (ORB0, Shift[1], SFI);
  and and_3 (ORB1, Shift[2], SFI);
  ROM #(.addrWidth(6), .dataWidth(30)) uROM (
    .addr(UADDR),
    .data({UWORD, RegSrc, ImmSrc, ALUSrc, ALUC_ROM, R2orImmtoReg, MemtoReg, RW, MW, BR, FLAGW, SFI}));
  Register #(.width(2)) ZN (.D(Flags[3:2]), .en(EN_NZ), .clk(CLK), .Q(NZCV));  // open: clr
  Register #(.width(2)) VC (.D(Flags[1:0]), .en(EN_CV), .clk(CLK), .Q(CVQ));  // open: clr
  and and_4 (WPC15, RW, RD15);
  or or_1 (BRANY, BR, WPC15);
  assign ALUControl = ALUC_ROM | {1'b0, ORB1, ORB0};  // OR_Gate or_2, 3 bits wide
  and and_5 (EN_NZ, FLAGW[1], cond_pass_dbg);
  and and_6 (EN_CV, FLAGW[0], cond_pass_dbg);
  and and_7 (PCSrc, BRANY, cond_pass_dbg);
  and and_8 (RegWrite, RW, cond_pass_dbg);
  and and_9 (MemWrite, MW, cond_pass_dbg);

  // Other names for the same wires on the sheet: NZCV[1:0] = CVQ; NZQ[1:0] = NZCV; ALUC_o[2:0] = ALUControl;
  //   CM = cond_pass_dbg; CVIN[1:0] = Flags[1:0]; NZIN[1:0] = Flags[3:2]; MW_o = MemWrite; ORBUS[1:0] = {ORB1, ORB0};
  //   PCSrc_o = PCSrc; RDb0 = Rd[0]; RDb1 = Rd[1]; RDb2 = Rd[2]; RDb3 = Rd[3]; RW_o = RegWrite; SH0 = Shift[0];
  //   SH1 = Shift[1]; SH2 = Shift[2];
  //   UWORD[16:0] = {RegSrc, ImmSrc, ALUSrc, ALUC_ROM, R2orImmtoReg, MemtoReg, RW, MW, BR, FLAGW, SFI};
  //   FW_VC = FLAGW[0]; FW_NZ = FLAGW[1]; M2R_o = MemtoReg; R2I_o = R2orImmtoReg; ALUSrc_o = ALUSrc;
  //   ImmSrc_o[1:0] = ImmSrc; RegSrc_o[2:0] = RegSrc

  // Notes on the sheet:
  //   contents of uROM (hex, n*v repeats v):
  //   00: 00000000 00000020 00000026 00004820 00004826 00000120 00000126 00004920 08: 00004926 00000220
  //   00000224 00004a20 00004a24 00000320 00000324 00004b20 10: 00004b24 00014ca0 00014ca4 00013c21
  //   00013c25 00000106 00004906 00001860 18: 00001810 0000a808 00001960 00001910 00000000 00000000
  //   00000000 00000000 20: 00000000 00000000 00000000 00000000 00000000 00000000 00000000 00000000 28:
  //   00000000 00000000 00000000 00000000 00000000 00000000 00000000 00000000 30: 00000000 00000000
  //   00000000 00000000 00000000 00000000 00000000 00000000 38: 00000000 00000000 00000000 00000000
  //   00000000 00000000 00000000 00000000
endmodule

module Extender (
  input  [1:0] ImmSrc,
  input  [23:0] In,
  output [31:0] Out
);

  wire [31:0] bit_extender_1_out, bit_extender_2_out, bit_extender_3_out, bit_extender_4_out;

  assign bit_extender_1_out = {{24{In[7]}}, In[7:0]};  // Bit_Extender bit_extender_1
  assign bit_extender_2_out = {{20{In[11]}}, In[11:0]};  // Bit_Extender bit_extender_2
  assign bit_extender_3_out = {{8{In[23]}}, In};  // Bit_Extender bit_extender_3
  assign bit_extender_4_out = {{27{In[11]}}, In[11:7]};  // Bit_Extender bit_extender_4
  Multiplexer #(.select(2), .width(32)) multiplexer_1 (
    .in0(bit_extender_1_out), .in1(bit_extender_2_out), .in2(bit_extender_3_out), .in3(bit_extender_4_out),
    .out(Out), .sel(ImmSrc));

  // Notes on the sheet:
  //   01: Zero-Extend Imm12 for ldr
  //   10: Sign-Extend imm22 for branch
  //   11: Zero-Extend Shamt5 for shifts
  //   00: Zero-Extend Imm8 for Arith-Logic
endmodule

module ALUw_Flags_7d6c4d71 (
  input  [2:0] ALUControl,
  input  [31:0] B,
  input  [31:0] A,
  output [31:0] Result,
  output [3:0] ALUFlags
);

  wire adder_1_cout, not_2_out, not_3_out, Sum31, xor_1_out, xor_2_out, xor_3_out;
  wire [30:0] adder_1_out;
  wire [31:0] and_1_out, multiplexer_1_out, negator_1_out, not_1_out, or_1_out, shifter_1_out, shifter_2_out,
       shifter_3_out;

  Multiplexer #(.width(32)) multiplexer_1 (.in0(B), .in1(not_1_out), .out(multiplexer_1_out), .sel(ALUControl[0]));
  assign not_1_out = ~B;  // NOT_Gate not_1, 32 bits wide
  not not_2 (not_2_out, ALUControl[1]);
  xor xor_1 (xor_1_out, B[31], A[31]);
  xor xor_2 (xor_2_out, xor_1_out, ALUControl[0]);
  xor xor_3 (xor_3_out, A[31], Sum31);
  Shifter_part #(.width(32)) shifter_1 (.in(A), .\dist (B[4:0]), .out(shifter_1_out));
  Shifter_part #(.shift("lr"), .width(32)) shifter_2 (.in(A), .\dist (B[4:0]), .out(shifter_2_out));
  Shifter_part #(.shift("ar"), .width(32)) shifter_3 (.in(A), .\dist (B[4:0]), .out(shifter_3_out));
  Negator #(.width(32)) negator_1 (.in(A), .out(negator_1_out));
  not not_3 (not_3_out, xor_2_out);
  Adder #(.width(32)) adder_1 (
    .a(multiplexer_1_out), .b(A), .out({Sum31, adder_1_out}), .cin(ALUControl[0]), .cout(adder_1_cout));
  assign and_1_out = B & A;  // AND_Gate and_1, 32 bits wide
  assign or_1_out = B | A;  // OR_Gate or_1, 32 bits wide
  and and_2 (ALUFlags[1], adder_1_cout, not_2_out);
  and and_3 (ALUFlags[0], not_2_out, not_3_out, xor_3_out);
  Multiplexer #(.select(3), .width(32)) multiplexer_2 (
    .in0({Sum31, adder_1_out}), .in1({Sum31, adder_1_out}), .in2(and_1_out), .in3(or_1_out),
    .in4(shifter_1_out), .in5(shifter_2_out), .in6(shifter_3_out), .in7(negator_1_out),
    .out({ALUFlags[3], Result[30:0]}), .sel(ALUControl));
  Comparator #(.width(32)) comparator_1 (
    .a({ALUFlags[3], Result[30:0]}), .b({32{1'b0}}), .eq(ALUFlags[2]));  // open: gt, lt

  assign Result[31] = ALUFlags[3];

  // Notes on the sheet:
  //   ALUControl1
  //   ALUControl0
  //   3 Input XNOR wegen Bug in XNOR
  //   Carry
  //   Overflow
  //   Zero
  //   Negative
endmodule

module Shifter (
  input  [1:0] ShiftCtrl,
  input  [4:0] Width,
  input  [31:0] A,
  output [31:0] Out
);

  wire [31:0] shifter_1_out, shifter_2_out, shifter_3_out, shifter_4_out;

  Shifter_part #(.width(32)) shifter_1 (.in(A), .\dist (Width), .out(shifter_1_out));
  Shifter_part #(.shift("lr"), .width(32)) shifter_2 (.in(A), .\dist (Width), .out(shifter_2_out));
  Shifter_part #(.shift("ar"), .width(32)) shifter_3 (.in(A), .\dist (Width), .out(shifter_3_out));
  Shifter_part #(.shift("rr"), .width(32)) shifter_4 (.in(A), .\dist (Width), .out(shifter_4_out));
  Multiplexer #(.select(2), .width(32)) multiplexer_1 (
    .in0(shifter_1_out), .in1(shifter_2_out), .in2(shifter_3_out), .in3(shifter_4_out), .out(Out),
    .sel(ShiftCtrl));
endmodule

module PCSrc (
  input  condMet,
  input  opt0,
  input  opt1,
  input  RD15,
  output PCSrc
);

  wire and_1_out, and_2_out, not_1_out, not_2_out, not_3_out, or_1_out;

  not not_1 (not_1_out, condMet);
  not not_2 (not_2_out, opt0);
  and and_1 (and_1_out, not_2_out, not_3_out);
  not not_3 (not_3_out, RD15);
  or or_1 (or_1_out, not_1_out, and_1_out);
  and and_2 (and_2_out, opt0, opt1);
  or or_2 (PCSrc, or_1_out, and_2_out);
endmodule

module IR (
  input  CLK,
  input  [31:0] D,
  input  IRWrite,
  output [31:0] Q
);

  wire [31:0] multiplexer_1_out;

  Register #(.width(32)) register_1 (.D(multiplexer_1_out), .clk(CLK), .Q(Q));  // open: en, clr
  Multiplexer #(.enable("true"), .width(32)) multiplexer_1 (
    .in0(Q), .in1(D), .out(multiplexer_1_out), .sel(IRWrite));  // open: en
endmodule

module NextPC (
  input  Sel0,
  input  [23:0] PC,
  input  [23:0] PCPlus1,
  input  [23:0] BranchTarget,
  input  [23:0] Extra,
  input  Sel1,
  output [23:0] NexPC
);

  wire [23:0] multiplexer_1_out, multiplexer_2_out;

  Multiplexer #(.enable("true"), .width(24)) multiplexer_1 (
    .in0(PC), .in1(PCPlus1), .out(multiplexer_1_out), .sel(Sel0));  // open: en
  Multiplexer #(.enable("true"), .width(24)) multiplexer_2 (
    .in0(BranchTarget), .in1(Extra), .out(multiplexer_2_out), .sel(Sel0));  // open: en
  Multiplexer #(.enable("true"), .width(24)) multiplexer_3 (
    .in0(multiplexer_1_out), .in1(multiplexer_2_out), .out(NexPC), .sel(Sel1));  // open: en
endmodule
